// Logisim project Slide08_FF_RS.circ as structural Verilog: 1 circuit, main circuit main
module main (
  output out_1
);

  wire clock_1_out, R_p1, S_p1;

  Clock clock_1 (.out(clock_1_out));
  // DipSwitch #(.NSwitches(1)) S: pin names not known; wires that end beside it: S_p1
  // DipSwitch #(.NSwitches(1)) R: pin names not known; wires that end beside it: R_p1
  S_R_Flip_Flop s_r_ff_1 (.S(S_p1), .clk(clock_1_out), .R(R_p1), .Q(out_1));  // open: Qn, preset, reset
endmodule
