// Logisim project Slide09_FF_RS_OSC_CLK.circ as structural Verilog: 1 circuit, main circuit main
module main (
  output out_1
);

  wire digital_oscilloscope_1_p1, digital_oscilloscope_1_p2, digital_oscilloscope_1_p3,
       digital_oscilloscope_1_p5;

  // Digital_Oscilloscope #(.nState(16)) digital_oscilloscope_1: pin names not known; wires that end beside it: digital_oscilloscope_1_p1, digital_oscilloscope_1_p2, digital_oscilloscope_1_p3, out_1, digital_oscilloscope_1_p5
  Clock CLK (.out(digital_oscilloscope_1_p1));
  Clock #(.highDuration(2), .lowDuration(2)) SET (.out(digital_oscilloscope_1_p2));
  Clock #(.highDuration(4), .lowDuration(4)) RESET (.out(digital_oscilloscope_1_p3));
  S_R_Flip_Flop s_r_ff_1 (
    .S(digital_oscilloscope_1_p2), .clk(digital_oscilloscope_1_p1), .R(digital_oscilloscope_1_p3), .Q(out_1));  // open: Qn, preset, reset
  Button button_1 (.out(digital_oscilloscope_1_p5));

  // Notes on the sheet:
  //   CLK
  //   SET
  //   RESET
  //   Q
endmodule
