// Logisim project Slide10_FF_JK.circ as structural Verilog: 1 circuit, main circuit main
module main (
  output out_1
);

  wire clock_1_out, J_p1, K_p1;

  Clock clock_1 (.out(clock_1_out));
  // DipSwitch #(.NSwitches(1)) J: pin names not known; wires that end beside it: J_p1
  // DipSwitch #(.NSwitches(1)) K: pin names not known; wires that end beside it: K_p1
  J_K_Flip_Flop j_k_ff_1 (.J(J_p1), .clk(clock_1_out), .K(K_p1), .Q(out_1));  // open: Qn, preset, reset
endmodule
