// Logisim project Slide11_FF_D.circ as structural Verilog: 1 circuit, main circuit main
module main (
  output out_1
);

  wire CLK_out, D_p1;

  Clock CLK (.out(CLK_out));
  // DipSwitch #(.NSwitches(1)) D: pin names not known; wires that end beside it: D_p1
  D_Flip_Flop d_ff_1 (.clk(CLK_out), .D(D_p1), .Q(out_1));  // open: Qn, preset, reset
endmodule
