// Logisim project Slide12_FF_T.circ as structural Verilog: 1 circuit, main circuit main
module main (
  output out_1
);

  wire CLK_out, T_p1;

  Clock CLK (.out(CLK_out));
  // DipSwitch #(.NSwitches(1)) T: pin names not known; wires that end beside it: T_p1
  T_Flip_Flop t_ff_1 (.clk(CLK_out), .T(T_p1), .Q(out_1));  // open: Qn, preset, reset
endmodule
