// Logisim project Slide13_FF_JK_OSC_CLK_PRECLR.circ as structural Verilog: 1 circuit, main circuit main
module main (
  output out_1
);

  wire digital_oscilloscope_1_p1, digital_oscilloscope_1_p4, digital_oscilloscope_1_p5, PRE_p1;

  // Digital_Oscilloscope #(.nState(16)) digital_oscilloscope_1: pin names not known; wires that end beside it: digital_oscilloscope_1_p1, 1'b1, 1'b1, digital_oscilloscope_1_p4, digital_oscilloscope_1_p5, out_1
  Clock CLK (.out(digital_oscilloscope_1_p1));
  // DipSwitch #(.NSwitches(1)) PRE: pin names not known; wires that end beside it: PRE_p1, digital_oscilloscope_1_p4
  // DipSwitch #(.NSwitches(1)) CLR: pin names not known; wires that end beside it: digital_oscilloscope_1_p5
  Button button_1 (.out(PRE_p1));
  J_K_Flip_Flop #(.trigger("falling"), .NegatePresetClear("true")) j_k_ff_1 (
    .J(1'b1), .clk(digital_oscilloscope_1_p1), .K(1'b1), .Q(out_1), .preset(digital_oscilloscope_1_p4),
    .reset(digital_oscilloscope_1_p5));  // open: Qn

  // Notes on the sheet:
  //   CLK
  //   J
  //   K
  //   PRE
  //   CLR
  //   Q
endmodule
