// Logisim project Contador_Síncrono.circ as structural Verilog: 1 circuit, main circuit main
module main (
  output out_1,
  output out_2,
  output out_3,
  output out_4,
  output out_5,
  output out_6,
  output out_7,
  output out_8
);

  wire and_1_out, and_2_out, and_3_out, and_4_out, and_5_out, and_6_out, clock_1_out;

  Clock clock_1 (.out(clock_1_out));
  T_Flip_Flop #(.trigger("falling")) t_ff_1 (.clk(clock_1_out), .T(1'b1), .Q(out_1));  // open: Qn, preset, reset
  T_Flip_Flop #(.trigger("falling")) t_ff_2 (.clk(clock_1_out), .T(out_1), .Q(out_2));  // open: Qn, preset, reset
  and and_1 (and_1_out, out_2, out_1);
  T_Flip_Flop #(.trigger("falling")) t_ff_3 (.clk(clock_1_out), .T(and_1_out), .Q(out_3));  // open: Qn, preset, reset
  and and_2 (and_2_out, out_3, out_2, out_1);
  T_Flip_Flop #(.trigger("falling")) t_ff_4 (.clk(clock_1_out), .T(and_2_out), .Q(out_4));  // open: Qn, preset, reset
  T_Flip_Flop #(.trigger("falling")) t_ff_5 (.clk(clock_1_out), .T(and_3_out), .Q(out_5));  // open: Qn, preset, reset
  and and_3 (and_3_out, out_4, out_3, out_2, out_1);
  T_Flip_Flop #(.trigger("falling")) t_ff_6 (.clk(clock_1_out), .T(and_4_out), .Q(out_6));  // open: Qn, preset, reset
  and and_4 (and_4_out, out_5, out_4, out_3, out_2, out_1);
  T_Flip_Flop #(.trigger("falling")) t_ff_7 (.clk(clock_1_out), .T(and_5_out), .Q(out_7));  // open: Qn, preset, reset
  and and_5 (and_5_out, out_6, out_5, out_4, out_3, out_2, out_1);
  T_Flip_Flop #(.trigger("falling")) t_ff_8 (.clk(clock_1_out), .T(and_6_out), .Q(out_8));  // open: Qn, preset, reset
  and and_6 (and_6_out, out_7, out_6, out_5, out_4, out_3, out_2, out_1);
endmodule
