// Logisim project DE0-CV.circ as structural Verilog: 2 circuits, main circuit main
module main (
);

  wire K0, K1, K2, K3, L0, L1, L2, L3, L4, L5, L6, L7, L8, L9, S0, S1, S2, S3, S4, S5, S6, S7, S8, S9;
  wire [3:0] HEX0, HEX1, HEX2, HEX3, HEX4, HEX5;

  Hex_Digit_Display hex_digit_display_1 (.value(HEX5));  // open: dp
  LED u_L8 (.in(L8));
  LED u_L9 (.in(L9));
  // DipSwitch #(.NSwitches(1)) S9: pin names not known; wires that end beside it: S9
  // DipSwitch #(.NSwitches(1)) S8: pin names not known; wires that end beside it: S8
  Hex_Digit_Display hex_digit_display_2 (.value(HEX4));  // open: dp
  Hex_Digit_Display hex_digit_display_3 (.value(HEX3));  // open: dp
  LED u_L6 (.in(L6));
  LED u_L5 (.in(L5));
  LED u_L7 (.in(L7));
  // DipSwitch #(.NSwitches(1)) S5: pin names not known; wires that end beside it: S5
  // DipSwitch #(.NSwitches(1)) S7: pin names not known; wires that end beside it: S7
  // DipSwitch #(.NSwitches(1)) S6: pin names not known; wires that end beside it: S6
  Hex_Digit_Display hex_digit_display_4 (.value(HEX2));  // open: dp
  LED u_L4 (.in(L4));
  LED u_L3 (.in(L3));
  // DipSwitch #(.NSwitches(1)) S3: pin names not known; wires that end beside it: S3
  // DipSwitch #(.NSwitches(1)) S4: pin names not known; wires that end beside it: S4
  // DipSwitch #(.NSwitches(1)) S2: pin names not known; wires that end beside it: S2
  Hex_Digit_Display hex_digit_display_5 (.value(HEX1));  // open: dp
  Hex_Digit_Display hex_digit_display_6 (.value(HEX0));  // open: dp
  LED u_L2 (.in(L2));
  LED u_L0 (.in(L0));
  LED u_L1 (.in(L1));
  // DipSwitch #(.NSwitches(1)) S0: pin names not known; wires that end beside it: S0
  // DipSwitch #(.NSwitches(1)) S1: pin names not known; wires that end beside it: S1
  \contador_síncrono  \contador_síncrono_1  ();  // open: in_2, out_3, in_1
  Button u_K2 (.out(K2));
  Button u_K3 (.out(K3));
  Button u_K1 (.out(K1));
  Button u_K0 (.out(K0));
endmodule

module \contador_síncrono  (
  input  in_1,
  input  in_2,
  output [7:0] out_3
);

  wire and_1_out, and_2_out, and_3_out, and_4_out, and_5_out, and_6_out;

  T_Flip_Flop #(.trigger("falling")) t_ff_1 (.clk(in_1), .T(1'b1), .Q(out_3[0]), .reset(in_2));  // open: Qn, preset
  T_Flip_Flop #(.trigger("falling")) t_ff_2 (.clk(in_1), .T(out_3[0]), .Q(out_3[1]), .reset(in_2));  // open: Qn, preset
  and and_1 (and_1_out, out_3[1], out_3[0]);
  T_Flip_Flop #(.trigger("falling")) t_ff_3 (
    .clk(in_1), .T(and_1_out), .Q(out_3[2]), .reset(in_2));  // open: Qn, preset
  and and_2 (and_2_out, out_3[2], and_1_out);
  T_Flip_Flop #(.trigger("falling")) t_ff_4 (
    .clk(in_1), .T(and_2_out), .Q(out_3[3]), .reset(in_2));  // open: Qn, preset
  and and_3 (and_3_out, out_3[3], and_2_out);
  T_Flip_Flop #(.trigger("falling")) t_ff_5 (
    .clk(in_1), .T(and_3_out), .Q(out_3[4]), .reset(in_2));  // open: Qn, preset
  and and_4 (and_4_out, out_3[4], and_3_out);
  T_Flip_Flop #(.trigger("falling")) t_ff_6 (
    .clk(in_1), .T(and_4_out), .Q(out_3[5]), .reset(in_2));  // open: Qn, preset
  and and_5 (and_5_out, out_3[5], and_4_out);
  T_Flip_Flop #(.trigger("falling")) t_ff_7 (
    .clk(in_1), .T(and_5_out), .Q(out_3[6]), .reset(in_2));  // open: Qn, preset
  and and_6 (and_6_out, out_3[6], and_5_out);
  T_Flip_Flop #(.trigger("falling")) t_ff_8 (.clk(in_1), .T(and_6_out), .Q(out_3[7]));  // open: Qn, preset, reset
endmodule
