// Logisim project DE0-CV.circ as structural Verilog: 1 circuit, main circuit main
module main (
);

  wire K0, K1, K2, K3, L0, L1, L2, L3, L4, L5, L6, L7, L8, L9, S0, S1, S2, S3, S4, S5, S6, S7, S8, S9;
  wire [3:0] HEX0, HEX1, HEX2, HEX3, HEX4, HEX5;

  Hex_Digit_Display hex_digit_display_1 (.value(HEX5));  // open: dp
  LED u_L8 (.in(L8));
  LED u_L9 (.in(L9));
  // DipSwitch #(.NSwitches(1)) S8: pin names not known; wires that end beside it: S8
  // DipSwitch #(.NSwitches(1)) S9: pin names not known; wires that end beside it: S9
  Hex_Digit_Display hex_digit_display_2 (.value(HEX3));  // open: dp
  Hex_Digit_Display hex_digit_display_3 (.value(HEX4));  // open: dp
  LED u_L6 (.in(L6));
  LED u_L7 (.in(L7));
  LED u_L5 (.in(L5));
  // DipSwitch #(.NSwitches(1)) S7: pin names not known; wires that end beside it: S7
  // DipSwitch #(.NSwitches(1)) S5: pin names not known; wires that end beside it: S5
  // DipSwitch #(.NSwitches(1)) S6: pin names not known; wires that end beside it: S6
  \contador_síncrono_main  main_1 (.in_1(S9), .in_2(S0), .out_3({L7, L6, L5, L4, L3, L2, L1, L0}));
  Hex_Digit_Display hex_digit_display_4 (.value(HEX2));  // open: dp
  LED u_L3 (.in(L3));
  LED u_L4 (.in(L4));
  // DipSwitch #(.NSwitches(1)) S2: pin names not known; wires that end beside it: S2
  // DipSwitch #(.NSwitches(1)) S4: pin names not known; wires that end beside it: S4
  // DipSwitch #(.NSwitches(1)) S3: pin names not known; wires that end beside it: S3
  Hex_Digit_Display hex_digit_display_5 (.value(HEX0));  // open: dp
  Hex_Digit_Display hex_digit_display_6 (.value(HEX1));  // open: dp
  LED u_L0 (.in(L0));
  LED u_L1 (.in(L1));
  LED u_L2 (.in(L2));
  // DipSwitch #(.NSwitches(1)) S1: pin names not known; wires that end beside it: S1
  // DipSwitch #(.NSwitches(1)) S0: pin names not known; wires that end beside it: S0
  ROM #(.dataWidth(16), .Select("low")) rom_1 (
    .addr({L7, L6, L5, L4, L3, L2, L1, L0}), .data({HEX5, HEX4, HEX3, HEX2}));
  Button u_K2 (.out(K2));
  Button u_K3 (.out(K3));
  Button u_K1 (.out(K1));
  Button u_K0 (.out(K0));
  // Digital_Oscilloscope #(.nState(16)) digital_oscilloscope_1: pin names not known; wires that end beside it: S9, L0, L1, L2, L3, L4, L5, L6, L7

  // Notes on the sheet:
  //   contents of rom_1 (hex, n*v repeats v):
  //   110 0 0 101 1001 1 0 1 110 10 0 10 110 11 0 100 0 1100 0 1000 13*0 100 0 0 110 0 0 1 1001 0 0 1 1001
  //   0 0 10 110 11 0 10 110 1 0 10 1001 11 0 10 110 10 0 0 110 0 0 1 0 1000
endmodule
