// Logisim project DE0-CV.circ as structural Verilog: 1 circuit, main circuit main
module main (
  input  in_1,
  input  in_2,
  input  [1:0] in_3
);

  wire K0, K1, K2, K3, L0, L1, L2, L3, L4, L5, L6, L7, S0, S1, S2, S3, S4, S5, S6, S7, S8, S9;
  wire [3:0] HEX0, HEX1, HEX2, HEX3, HEX4, HEX5, ULA_out_4;

  Hex_Digit_Display hex_digit_display_1 (.value(HEX5));  // open: dp
  LED L9 (.in(in_3[1]));
  LED L8 (.in(in_3[0]));
  // DipSwitch #(.NSwitches(1)) S8: pin names not known; wires that end beside it: S8
  // DipSwitch #(.NSwitches(1)) S9: pin names not known; wires that end beside it: S9
  Hex_Digit_Display hex_digit_display_2 (.value(HEX3));  // open: dp
  Hex_Digit_Display hex_digit_display_3 (.value(HEX4));  // open: dp
  LED u_L5 (.in(L5));
  LED u_L7 (.in(L7));
  LED u_L6 (.in(L6));
  // DipSwitch #(.NSwitches(1)) S6: pin names not known; wires that end beside it: S6
  // DipSwitch #(.NSwitches(1)) S5: pin names not known; wires that end beside it: S5
  // DipSwitch #(.NSwitches(1)) S7: pin names not known; wires that end beside it: S7
  \contador_síncrono_main  main_1 (.in_1(S9), .in_2(S0), .out_3({L7, L6, L5, L4, L3, L2, L1, L0}));
  Hex_Digit_Display hex_digit_display_4 (.value(HEX2));  // open: dp
  LED u_L4 (.in(L4));
  LED u_L3 (.in(L3));
  // DipSwitch #(.NSwitches(1)) S3: pin names not known; wires that end beside it: S3
  // DipSwitch #(.NSwitches(1)) S2: pin names not known; wires that end beside it: S2
  // DipSwitch #(.NSwitches(1)) S4: pin names not known; wires that end beside it: S4
  Hex_Digit_Display hex_digit_display_5 (.value(HEX0));  // open: dp
  Hex_Digit_Display hex_digit_display_6 (.value(HEX1));  // open: dp
  LED u_L0 (.in(L0));
  LED u_L1 (.in(L1));
  LED u_L2 (.in(L2));
  // DipSwitch #(.NSwitches(1)) S1: pin names not known; wires that end beside it: S1
  // DipSwitch #(.NSwitches(1)) S0: pin names not known; wires that end beside it: S0
  ROM #(.dataWidth(16), .Select("low")) rom_1 (
    .addr({L7, L6, L5, L4, L3, L2, L1, L0}), .data({HEX5, HEX4, HEX3, HEX2}));
  Button u_K3 (.out(K3));
  Button u_K2 (.out(K2));
  Button u_K1 (.out(K1));
  Button u_K0 (.out(K0));
  // Digital_Oscilloscope #(.nState(16)) digital_oscilloscope_1: pin names not known
  ula_main ULA (.E1({S4, S3, S2, S1}), .E2({S8, S7, S6, S5}), .out_4(ULA_out_4), .OP(in_3));
  registrador_paralelo_main REG_1 (.in_1(in_1), .in_2(S0), .in_3(S9), .in_4(ULA_out_4), .out_5(HEX1));
  registrador_paralelo_main REG2 (.in_1(in_2), .in_2(S0), .in_3(S9), .in_4(ULA_out_4), .out_5(HEX0));

  // Other names for the same wires on the sheet: L8 = in_3[0]; OP[1:0] = in_3; L9 = in_3[1]

  // Notes on the sheet:
  //   contents of rom_1 (hex, n*v repeats v):
  //   6005 9101 6202 6304 c08 0 0 0 400 6001 9001 9002 6302 6102 9302 6200 6001 800
endmodule
