// Logisim project registrador_paralelo.circ as structural Verilog: 1 circuit, main circuit main
module main (
  input  in_1,
  input  in_2,
  input  in_3,
  input  [3:0] in_4,
  output [3:0] out_5
);

  wire multiplexer_1_out, multiplexer_2_out, multiplexer_3_out, multiplexer_4_out;

  Multiplexer #(.enable("false")) multiplexer_1 (.in0(out_5[0]), .in1(in_4[0]), .out(multiplexer_1_out), .sel(in_1));
  D_Flip_Flop d_ff_1 (.clk(in_3), .D(multiplexer_1_out), .Q(out_5[0]), .reset(in_2));  // open: Qn, preset
  D_Flip_Flop d_ff_2 (.clk(in_3), .D(multiplexer_2_out), .Q(out_5[1]), .reset(in_2));  // open: Qn, preset
  Multiplexer #(.enable("false")) multiplexer_2 (.in0(out_5[1]), .in1(in_4[1]), .out(multiplexer_2_out), .sel(in_1));
  Multiplexer #(.enable("false")) multiplexer_3 (.in0(out_5[2]), .in1(in_4[2]), .out(multiplexer_3_out), .sel(in_1));
  D_Flip_Flop d_ff_3 (.clk(in_3), .D(multiplexer_3_out), .Q(out_5[2]), .reset(in_2));  // open: Qn, preset
  Multiplexer #(.enable("false")) multiplexer_4 (.in0(out_5[3]), .in1(in_4[3]), .out(multiplexer_4_out), .sel(in_1));
  D_Flip_Flop d_ff_4 (.clk(in_3), .D(multiplexer_4_out), .Q(out_5[3]), .reset(in_2));  // open: Qn, preset

  // Other names for the same wires on the sheet: CLEAR = in_2; CLK = in_3; D0 = in_4[0]; D1 = in_4[1]; D2 = in_4[2];
  //   D3 = in_4[3]; S0 = out_5[0]; S1 = out_5[1]; S2 = out_5[2]; S3 = out_5[3]; SET = in_1
endmodule
