// Logisim project ula.circ as structural Verilog: 1 circuit, main circuit main
module main (
  input  [3:0] E1,
  input  [3:0] E2,
  input  [1:0] OP,
  output [3:0] out_4
);

  wire [3:0] adder_1_out, divider_1_out, multiplier_1_out, subtractor_1_out;

  Multiplier #(.width(4)) multiplier_1 (.a(E1), .b(4'b0010), .out(multiplier_1_out));  // open: cin, cout
  Subtractor #(.width(4)) subtractor_1 (.a(E1), .b(E2), .out(subtractor_1_out));  // open: bin, bout
  Adder #(.width(4)) adder_1 (.a(E1), .b(E2), .out(adder_1_out));  // open: cin, cout
  Divider #(.width(4)) divider_1 (.a(E1), .b(4'b0010), .out(divider_1_out));  // open: upper, rem
  Multiplexer #(.select(2), .width(4), .enable("false")) multiplexer_1 (
    .in0(adder_1_out), .in1(multiplier_1_out), .in2(subtractor_1_out), .in3(divider_1_out), .out(out_4),
    .sel(OP));
  Hex_Digit_Display hex_digit_display_1 (.value(out_4));  // open: dp
endmodule
