// Logisim project DE0-CV.circ as structural Verilog: 7 circuits, main circuit CPU
module CPU (
);

  wire and_1_out, and_2_out, CLEAR, JUMP, K0, K1, K2, K3, L8, L9, not_1_out, not_2_out, or_1_out, or_2_out,
       or_3_out, REALIZAR_OP, RESET, RgTO, S0, S1, S2, S3, S4, S5, S6, S7, S8, S9;
  wire [1:0] ULA;
  wire [3:0] HEX0, HEX1, HEX2, HEX3, HEX4, HEX5, OPERANDO, REG1, REG2, RgIN, ula4_1_out_4;
  wire [7:0] Count8, ENDERECO;

  Hex_Digit_Display hex_digit_display_1 (.value(HEX5));  // open: dp
  LED u_L8 (.in(L8));
  LED u_L9 (.in(L9));
  // DipSwitch #(.NSwitches(1)) S9: pin names not known; wires that end beside it: S9
  // DipSwitch #(.NSwitches(1)) S8: pin names not known; wires that end beside it: S8
  Hex_Digit_Display hex_digit_display_2 (.value(HEX3));  // open: dp
  Hex_Digit_Display hex_digit_display_3 (.value(HEX4));  // open: dp
  LED L6 (.in(Count8[6]));
  LED L7 (.in(Count8[7]));
  LED L5 (.in(Count8[5]));
  // DipSwitch #(.NSwitches(1)) S6: pin names not known; wires that end beside it: S6
  // DipSwitch #(.NSwitches(1)) S7: pin names not known; wires that end beside it: S7
  // DipSwitch #(.NSwitches(1)) S5: pin names not known; wires that end beside it: S5
  Hex_Digit_Display hex_digit_display_4 (.value(HEX2));  // open: dp
  LED L3 (.in(Count8[3]));
  LED L4 (.in(Count8[4]));
  // DipSwitch #(.NSwitches(1)) S4: pin names not known; wires that end beside it: S4
  // DipSwitch #(.NSwitches(1)) S3: pin names not known; wires that end beside it: S3
  // DipSwitch #(.NSwitches(1)) S2: pin names not known; wires that end beside it: S2
  Hex_Digit_Display hex_digit_display_5 (.value(HEX1));  // open: dp
  Hex_Digit_Display hex_digit_display_6 (.value(HEX0));  // open: dp
  LED L1 (.in(Count8[1]));
  LED L0 (.in(Count8[0]));
  LED L2 (.in(Count8[2]));
  // DipSwitch #(.NSwitches(1)) S1: pin names not known; wires that end beside it: S1
  // DipSwitch #(.NSwitches(1)) S0: pin names not known; wires that end beside it: S0
  Button u_K2 (.out(K2));
  Button u_K3 (.out(K3));
  Button u_K1 (.out(K1));
  Button u_K0 (.out(K0));
  or or_1 (or_1_out, RESET, S0);
  Count8 count8_1 (.CLK(S9), .out_5(Count8), .CLEAR(or_1_out), .JUMP(JUMP), .ENDERECO_JUMP(ENDERECO));
  UC uc_1 (
    .ROM({HEX5, HEX4, HEX3, HEX2}), .Rg1(HEX1), .Rg2(HEX0), .OPERANDO(OPERANDO), .ULA(ULA), .JUMP(JUMP),
    .ENDERECO_JUMP(ENDERECO), .RgIN(RgIN), .RgTO(RgTO), .CLEAR_REG(CLEAR), .RESET(RESET),
    .FAZER_OP(REALIZAR_OP));
  not not_1 (not_1_out, S9);
  ROM256x16 rom256x16_1 (.CLK(not_1_out), .in_2(Count8), .out_3({HEX5, HEX4, HEX3, HEX2}));
  ULA4 ula4_1 (.E1(OPERANDO), .E2(RgIN), .out_4(ula4_1_out_4), .OP(ULA));
  Demultiplexer #(.width(4), .enable("false")) demultiplexer_1 (
    .out0(REG1), .out1(REG2), .in(ula4_1_out_4), .sel(RgTO));
  and and_1 (and_1_out, REALIZAR_OP, not_2_out);
  not not_2 (not_2_out, RgTO);
  or or_2 (or_2_out, CLEAR, S0);
  and and_2 (and_2_out, REALIZAR_OP, RgTO);
  or or_3 (or_3_out, CLEAR, S0);
  Reg4 reg4_1 (.in_1(and_1_out), .in_2(or_2_out), .in_3(S9), .in_4(REG1), .out_5(HEX1));
  Reg4 reg4_2 (.in_1(and_2_out), .in_2(or_3_out), .in_3(S9), .in_4(REG2), .out_5(HEX0));

  // Other names for the same wires on the sheet: L0 = Count8[0]; L1 = Count8[1]; L2 = Count8[2]; L3 = Count8[3];
  //   L4 = Count8[4]; L5 = Count8[5]; L6 = Count8[6]; L7 = Count8[7]; Rg1[3:0] = HEX1; Rg2[3:0] = HEX0;
  //   ROM[15:0] = {HEX5, HEX4, HEX3, HEX2}
endmodule

module ULA4 (
  input  [3:0] E1,
  input  [3:0] E2,
  input  [1:0] OP,
  output [3:0] out_4
);

  wire [3:0] adder_1_out, divider_1_out, multiplier_1_out, subtractor_1_out;

  Multiplier #(.width(4)) multiplier_1 (.a(E1), .b(4'b0010), .out(multiplier_1_out));  // open: cin, cout
  Subtractor #(.width(4)) subtractor_1 (.a(E2), .b(E1), .out(subtractor_1_out));  // open: bin, bout
  Adder #(.width(4)) adder_1 (.a(E2), .b(E1), .out(adder_1_out));  // open: cin, cout
  Divider #(.width(4)) divider_1 (.a(E1), .b(4'b0010), .out(divider_1_out));  // open: upper, rem
  Multiplexer #(.select(2), .width(4), .enable("false")) multiplexer_1 (
    .in0(adder_1_out), .in1(multiplier_1_out), .in2(subtractor_1_out), .in3(divider_1_out), .out(out_4),
    .sel(OP));
  Hex_Digit_Display hex_digit_display_1 (.value(out_4));  // open: dp
endmodule

module Count8 (
  input  CLK,
  input  CLEAR,
  input  JUMP,
  input  [7:0] ENDERECO_JUMP,
  output [7:0] out_5
);

  wire and_1_out, and_2_out, and_3_out, and_4_out, and_5_out, and_6_out, and_7_out, and_8_out, and_9_out,
       and_10_out, and_11_out, and_12_out, and_13_out, and_14_out, CLEAR_t, E0, E1, E2, E3, E4, E5, E6, E7,
       nand_1_out, nand_2_out, nand_3_out, nand_4_out, nand_5_out, nand_6_out, nand_7_out, nand_8_out,
       not_1_out, not_3_out, not_4_out, not_5_out, not_6_out, not_7_out, not_8_out, not_9_out, not_10_out,
       not_11_out, or_1_out, or_2_out, or_3_out, or_4_out, or_5_out, or_6_out, or_7_out, or_8_out;

  nand nand_1 (nand_1_out, E0, JUMP);
  and and_1 (and_1_out, or_1_out, CLEAR_t);
  or or_1 (or_1_out, E0, not_1_out);
  not not_1 (not_1_out, JUMP);
  not not_2 (CLEAR_t, CLEAR);
  T_Flip_Flop #(.NegatePresetClear("true")) t_ff_1 (
    .clk(CLK), .T(1'b1), .Q(out_5[0]), .preset(nand_1_out), .reset(and_1_out));  // open: Qn
  or or_2 (or_2_out, E1, not_5_out);
  not not_3 (not_3_out, CLEAR_t);
  not not_4 (not_4_out, CLEAR_t);
  nand nand_2 (nand_2_out, E1, JUMP);
  T_Flip_Flop #(.NegatePresetClear("true")) t_ff_2 (
    .clk(CLK), .T(out_5[0]), .Q(out_5[1]), .preset(nand_2_out), .reset(and_2_out));  // open: Qn
  and and_2 (and_2_out, or_2_out, CLEAR_t);
  not not_5 (not_5_out, JUMP);
  Reg4 reg4_1 (.in_1(JUMP), .in_2(not_3_out), .in_3(CLK), .in_4(ENDERECO_JUMP[3:0]), .out_5({E3, E2, E1, E0}));
  Reg4 reg4_2 (.in_1(JUMP), .in_2(not_4_out), .in_3(CLK), .in_4(ENDERECO_JUMP[7:4]), .out_5({E7, E6, E5, E4}));
  nand nand_3 (nand_3_out, E2, JUMP);
  T_Flip_Flop #(.NegatePresetClear("true")) t_ff_3 (
    .clk(CLK), .T(and_3_out), .Q(out_5[2]), .preset(nand_3_out), .reset(and_4_out));  // open: Qn
  and and_3 (and_3_out, out_5[1], out_5[0]);
  and and_4 (and_4_out, or_3_out, CLEAR_t);
  or or_3 (or_3_out, E2, not_6_out);
  not not_6 (not_6_out, JUMP);
  and and_5 (and_5_out, out_5[2], and_3_out);
  or or_4 (or_4_out, E3, not_7_out);
  nand nand_4 (nand_4_out, E3, JUMP);
  T_Flip_Flop #(.NegatePresetClear("true")) t_ff_4 (
    .clk(CLK), .T(and_5_out), .Q(out_5[3]), .preset(nand_4_out), .reset(and_6_out));  // open: Qn
  and and_6 (and_6_out, or_4_out, CLEAR_t);
  not not_7 (not_7_out, JUMP);
  nand nand_5 (nand_5_out, E4, JUMP);
  T_Flip_Flop #(.NegatePresetClear("true")) t_ff_5 (
    .clk(CLK), .T(and_7_out), .Q(out_5[4]), .preset(nand_5_out), .reset(and_8_out));  // open: Qn
  and and_7 (and_7_out, out_5[3], and_5_out);
  and and_8 (and_8_out, or_5_out, CLEAR_t);
  or or_5 (or_5_out, E4, not_8_out);
  not not_8 (not_8_out, JUMP);
  and and_9 (and_9_out, out_5[4], and_7_out);
  or or_6 (or_6_out, E5, not_9_out);
  nand nand_6 (nand_6_out, E5, JUMP);
  T_Flip_Flop #(.NegatePresetClear("true")) t_ff_6 (
    .clk(CLK), .T(and_9_out), .Q(out_5[5]), .preset(nand_6_out), .reset(and_10_out));  // open: Qn
  and and_10 (and_10_out, or_6_out, CLEAR_t);
  not not_9 (not_9_out, JUMP);
  nand nand_7 (nand_7_out, E6, JUMP);
  T_Flip_Flop #(.NegatePresetClear("true")) t_ff_7 (
    .clk(CLK), .T(and_11_out), .Q(out_5[6]), .preset(nand_7_out), .reset(and_12_out));  // open: Qn
  and and_11 (and_11_out, out_5[5], and_9_out);
  and and_12 (and_12_out, or_7_out, CLEAR_t);
  or or_7 (or_7_out, E6, not_10_out);
  not not_10 (not_10_out, JUMP);
  and and_13 (and_13_out, out_5[6], and_11_out);
  or or_8 (or_8_out, E7, not_11_out);
  nand nand_8 (nand_8_out, E7, JUMP);
  T_Flip_Flop #(.NegatePresetClear("true")) t_ff_8 (
    .clk(CLK), .T(and_13_out), .Q(out_5[7]), .preset(nand_8_out), .reset(and_14_out));  // open: Qn
  and and_14 (and_14_out, or_8_out, CLEAR_t);
  not not_11 (not_11_out, JUMP);

  // Other names for the same wires on the sheet: OUT0 = out_5[0]; OUT1 = out_5[1]; OUT2 = out_5[2]; OUT3 = out_5[3];
  //   OUT4 = out_5[4]; OUT5 = out_5[5]; OUT6 = out_5[6]; OUT7 = out_5[7]
endmodule

module Reg4 (
  input  in_1,
  input  in_2,
  input  in_3,
  input  [3:0] in_4,
  output [3:0] out_5
);

  wire multiplexer_1_out, multiplexer_2_out, multiplexer_3_out, multiplexer_4_out;

  Multiplexer #(.enable("false")) multiplexer_1 (.in0(out_5[0]), .in1(in_4[0]), .out(multiplexer_1_out), .sel(in_1));
  D_Flip_Flop d_ff_1 (.clk(in_3), .D(multiplexer_1_out), .Q(out_5[0]), .reset(in_2));  // open: Qn, preset
  D_Flip_Flop d_ff_2 (.clk(in_3), .D(multiplexer_2_out), .Q(out_5[1]), .reset(in_2));  // open: Qn, preset
  Multiplexer #(.enable("false")) multiplexer_2 (.in0(out_5[1]), .in1(in_4[1]), .out(multiplexer_2_out), .sel(in_1));
  Multiplexer #(.enable("false")) multiplexer_3 (.in0(out_5[2]), .in1(in_4[2]), .out(multiplexer_3_out), .sel(in_1));
  D_Flip_Flop d_ff_3 (.clk(in_3), .D(multiplexer_3_out), .Q(out_5[2]), .reset(in_2));  // open: Qn, preset
  Multiplexer #(.enable("false")) multiplexer_4 (.in0(out_5[3]), .in1(in_4[3]), .out(multiplexer_4_out), .sel(in_1));
  D_Flip_Flop d_ff_4 (.clk(in_3), .D(multiplexer_4_out), .Q(out_5[3]), .reset(in_2));  // open: Qn, preset

  // Other names for the same wires on the sheet: CLEAR = in_2; CLK = in_3; D0 = in_4[0]; D1 = in_4[1]; D2 = in_4[2];
  //   D3 = in_4[3]; S0 = out_5[0]; S1 = out_5[1]; S2 = out_5[2]; S3 = out_5[3]; SET = in_1
endmodule

module ROM256x16 (
  input  CLK,
  input  [7:0] in_2,
  output [15:0] out_3
);

  wire [15:0] rom_1_data;

  ROM #(.dataWidth(16), .Select("low")) rom_1 (.addr(in_2), .data(rom_1_data));
  Reg16 reg16_1 (.in_1(1'b1), .in_2(1'b0), .in_3(CLK), .in_4(rom_1_data), .out_5(out_3));

  // Notes on the sheet:
  //   contents of rom_1 (hex, n*v repeats v):
  //   6004 9102 6201 6305 9002 6002 9003 400 c0d 4*0 9002 6302 6101 9302 6200 6003 800
endmodule

module Reg16 (
  input  in_1,
  input  in_2,
  input  in_3,
  input  [15:0] in_4,
  output [15:0] out_5
);

  Reg4 reg4_1 (.in_1(in_1), .in_2(in_2), .in_3(in_3), .in_4(in_4[3:0]), .out_5(out_5[3:0]));
  Reg4 reg4_2 (.in_1(in_1), .in_2(in_2), .in_3(in_3), .in_4(in_4[7:4]), .out_5(out_5[7:4]));
  Reg4 reg4_3 (.in_1(in_1), .in_2(in_2), .in_3(in_3), .in_4(in_4[11:8]), .out_5(out_5[11:8]));
  Reg4 reg4_4 (.in_1(in_1), .in_2(in_2), .in_3(in_3), .in_4(in_4[15:12]), .out_5(out_5[15:12]));

  // Other names for the same wires on the sheet: CLEAR = in_2; CLK = in_3; IN1[3:0] = in_4[3:0]; IN2[3:0] = in_4[7:4];
  //   IN3[3:0] = in_4[11:8]; IN4[3:0] = in_4[15:12]; SET = in_1
endmodule

module UC (
  input  [15:0] ROM,
  input  [3:0] Rg1,
  input  [3:0] Rg2,
  output [3:0] OPERANDO,
  output [1:0] ULA,
  output FAZER_OP,
  output JUMP,
  output [7:0] ENDERECO_JUMP,
  output [3:0] RgIN,
  output RgTO,
  output CLEAR_REG,
  output RESET
);

  wire not_1_out, not_2_out, not_3_out, not_4_out;

  not not_1 (not_1_out, ROM[10]);
  not not_2 (not_2_out, ROM[11]);
  not not_3 (not_3_out, ROM[11]);
  not not_4 (not_4_out, ROM[10]);
  and and_1 (FAZER_OP, not_1_out, not_2_out);
  and and_2 (CLEAR_REG, ROM[10], not_3_out);
  and and_3 (RESET, not_4_out, ROM[11]);
  and and_4 (JUMP, ROM[10], ROM[11]);
  Multiplexer #(.width(4), .enable("false")) multiplexer_1 (
    .in0(4'b0000), .in1(ROM[3:0]), .out(OPERANDO), .sel(FAZER_OP));
  Multiplexer #(.width(2), .enable("false")) multiplexer_2 (.in0(2'b00), .in1(ROM[9:8]), .out(ULA), .sel(FAZER_OP));
  Multiplexer #(.width(8), .enable("false")) multiplexer_3 (
    .in0({8{1'b0}}), .in1({4'b0000, ROM[3:0]}), .out(ENDERECO_JUMP), .sel(JUMP));
  Multiplexer #(.select(2), .width(4), .enable("false")) multiplexer_4 (
    .in0(4'b0000), .in1(Rg1), .in2(Rg2), .in3(4'b0000), .out(RgIN), .sel(ROM[13:12]));
  Multiplexer #(.select(2), .enable("false")) multiplexer_5 (
    .in0(1'b0), .in1(1'b0), .in2(1'b1), .in3(1'b0), .out(RgTO), .sel(ROM[15:14]));

  // Other names for the same wires on the sheet: OPERANDO_t[3:0] = ROM[3:0]; JMP[1:0] = ROM[11:10];
  //   REALIZAR_OP = FAZER_OP; RgIN_t[1:0] = ROM[13:12]; RgTO_t[1:0] = ROM[15:14]; ULA_t[1:0] = ROM[9:8]
endmodule
